# Fritzing sketch circuit (saved by Fritzing 0.9.3b)
breadboards: 1

parts:
  パーツ1 = HX711 Weighing Sensor Module
  パーツ2 = SRF05 Ultrasonic Rangefinder
  Load_Cell1 = Load Cell - Red/white/black/green
  Raspberry_Pi_1 = Raspberry Pi 3 [part_number=RPI-3-V1.2]
  LED1 = LED - 5mm [color="Green (570nm)" package="5 mm [THT]"]
  LED2 = LED - 5mm [color="Blue (525nm)" package="5 mm [THT]"]
  LED3 = LED - 5mm [color="Red (633nm)" package="5 mm [THT]"]
  R1 = Resistor [tolerance=±5% resistance=220 package=THT]
  R2 = Resistor [tolerance=±5% resistance=220 package=THT]
  R3 = Resistor [tolerance=±5% resistance=220 package=THT]

nets:
  N1: パーツ1.VCC, Load_Cell1.wire1
  N2: パーツ1.GND, Load_Cell1.wire4
  N3: パーツ1.DO/RX, Load_Cell1.wire2
  N4: パーツ1.CK/TX, Load_Cell1.wire3
  VCC: パーツ1.E+, パーツ2.VCC, Raspberry_Pi_1.5V
  N5: パーツ1.E-, Raspberry_Pi_1.GPIO6
  N6: パーツ1.A+, Raspberry_Pi_1.GPIO13
  GND: パーツ1.B-, パーツ2.GND, Raspberry_Pi_1.GND, LED1.cathode, LED2.cathode, LED3.cathode
  N7: パーツ2.Trig, Raspberry_Pi_1.GPIO27
  N8: パーツ2.Echo, Raspberry_Pi_1.GPIO17
  N9: Raspberry_Pi_1.GPIO21, R1.Pin_1
  N10: Raspberry_Pi_1.GPIO20, R2.Pin_1
  N11: Raspberry_Pi_1.GPIO16, R3.Pin_1
  N12: LED1.anode, R1.Pin_0
  N13: LED2.anode, R2.Pin_0
  N14: LED3.anode, R3.Pin_0

custom parts:
  Load Cell - Red/white/black/green: A rectangle load cell/weighting pressure Sensor with four wires - Red, white, black, green. Normally corresponding with E+, E-, A+, A- respectively.
